# Fritzing sketch Esquema_Conexiones (saved by Fritzing 0.9.3b)

parts:
  Componente1 = Arduino Uno (Rev3)
  microSD_Transflash1 = SparkFun - microSD Transflash
  SP1 = SPEAKER [package=pcb_mount_speaker]
  GSM_SIM_GPSR_SMS_SIM900_SIM1 = SIM800L [package=THT]

nets:
  N1: Componente1.D8, GSM_SIM_GPSR_SMS_SIM900_SIM1.SIM_RXD
  N2: Componente1.D9_PWM, GSM_SIM_GPSR_SMS_SIM900_SIM1.SIM_TXD
  N3: Componente1.D10_PWM/SS, microSD_Transflash1.VCC
  N4: Componente1.D11_PWM/MOSI, microSD_Transflash1.DI
  GND: Componente1.GND, microSD_Transflash1.DO, GSM_SIM_GPSR_SMS_SIM900_SIM1.GND
  N5: Componente1.5V, microSD_Transflash1.CS
  N6: microSD_Transflash1.CD, SP1.+
  N7: microSD_Transflash1.GND, SP1.-
